# Fritzing sketch three-potentiometers (saved by Fritzing 0.8.7b)
breadboards: 1

parts:
  R1 = Resistor [tolerance=±5% resistance=330 package=THT]
  R2 = Resistor [tolerance=±5% resistance=330 package=THT]
  R3 = Resistor [tolerance=±5% resistance=330 package=THT]
  LED2 = RGB LED (com. cathode, rgb) [package="5 mm [THT]"]
  Part1 = Arduino Uno (Rev3)
  R5 = Rotary Potentiometer (Large) [maximum_resistance=100kΩ package=THT]
  R6 = Rotary Potentiometer (Large) [maximum_resistance=100kΩ package=THT]
  R4 = Rotary Potentiometer (Large) [package=THT]

nets:
  N1: R1.Pin_0, LED2.red_anode
  N2: R1.Pin_1, Part1.D9_PWM
  N3: R2.Pin_0, LED2.green_anode
  N4: R2.Pin_1, Part1.D10_PWM/SS
  N5: R3.Pin_0, LED2.blue_anode
  N6: R3.Pin_1, Part1.D11_PWM/MOSI
  N7: LED2.common_cathode, Part1.GND, R5.leg2, R6.leg2, R4.leg2
  N8: Part1.A0, R6.wiper
  N9: Part1.A1, R5.wiper
  N10: Part1.A2, R4.wiper
  N11: Part1.5V, R5.leg1, R6.leg1, R4.leg1

custom parts:
  RGB LED (com. cathode, rgb): A 5mm tri-color LED with red, green and blue inside.
