# Fritzing sketch just-the-led-please (saved by Fritzing 0.8.7b)
breadboards: 1

parts:
  R1 = Resistor [tolerance=±5% resistance=330 package=THT]
  R2 = Resistor [tolerance=±5% resistance=330 package=THT]
  R3 = Resistor [tolerance=±5% resistance=330 package=THT]
  LED2 = RGB LED (com. cathode, rgb) [package="5 mm [THT]"]
  Part1 = Arduino Uno (Rev3)

nets:
  N1: R1.Pin_0, LED2.red_anode
  N2: R2.Pin_0, LED2.green_anode
  N3: R3.Pin_0, LED2.blue_anode
  N4: R3.Pin_1, Part1.5V
  N5: LED2.common_cathode, Part1.GND

custom parts:
  RGB LED (com. cathode, rgb): A 5mm tri-color LED with red, green and blue inside.
